# Fritzing sketch bluetoorh car (saved by Fritzing 0.9.3b)

parts:
  元件1 = Arduino Nano (Rev3.0)
  U1 = L9110 H-bridge module [part_number="L9110 H-bridge"]
  M1 = DC Motor
  M2 = DC Motor
  元件2 = Bluetooth HC-05 Macho
  S1 = Round Pushbutton
  VCC1 = Battery
  元件3 = TP4056 Charger
  LM1 = RioRand LM2596
  U2 = Mini-360 DC-DC Buck converter [package=THT]

nets:
  GND: 元件1.GND, 元件2.GND, LM1.Pin_3
  N1: 元件1.D2, U1.A-IB
  N2: 元件1.D3, U1.A-IA
  N3: 元件1.D4, U1.B-IB
  N4: 元件1.D5, U1.B-IA
  N5: 元件1.D10, 元件2.TXD
  N6: 元件1.D11/MOSI, 元件2.RXD
  5V: 元件1.5V, 元件2.VCC, LM1.Pin_2
  N7: U1.GND, U2.OUT-
  N8: U1.VCC, U2.OUT+
  N9: U1.MOTOR_A-A, M2.pin_2
  N10: U1.MOTOR_A-B, M2.pin_1
  N11: U1.MOTOR_B-A, M1.pin_2
  N12: U1.MOTOR_B-B, M1.pin_1
  N13: S1.leg0, LM1.Pin_1
  N14: S1.leg1, VCC1.-
  N15: VCC1.+, 元件3.BAT+
  N16: LM1.Pin_0, U2.IN+

custom parts:
  Mini-360 DC-DC Buck converter: Mini-360 DC-DC Buck converter. Tiny buck step down voltage converter, input voltage 4.75 to 23V output 1 to 17V adjustable. Available from ebay and the like.
